// Logisim project pipe_blocks.circ as structural Verilog: 2 circuits, main circuit ALU
module ALU (
  input  [31:0] A,
  input  [31:0] B,
  input  [3:0] ALUCtl,
  output [31:0] ALUResult,
  output Zero
);

  wire [0:0] comparator_1_lt;
  wire [31:0] adder_1_out, AND_out, NOR_out, OR_out, subtractor_1_out, XOR_out;

  assign AND_out = A & B;  // AND_Gate AND, 32 bits wide
  assign OR_out = A | B;  // OR_Gate OR, 32 bits wide
  Adder #(.width(32)) adder_1 (.a(A), .b(B), .out(adder_1_out));  // open: cin, cout
  Subtractor #(.width(32)) subtractor_1 (.a(A), .b(B), .out(subtractor_1_out));  // open: bin, bout
  Comparator #(.width(32)) comparator_1 (.a(A), .b(B), .lt(comparator_1_lt[0]));  // open: gt, eq
  assign NOR_out = ~(A | B);  // NOR_Gate NOR, 32 bits wide
  assign XOR_out = A ^ B;  // XOR_Gate XOR, 32 bits wide
  Multiplexer #(.select(4), .width(32), .enable("false")) multiplexer_1 (
    .in0(AND_out), .in1(OR_out), .in2(adder_1_out), .in6(subtractor_1_out),
    .in7({{31{1'b0}}, comparator_1_lt[0]}), .in12(NOR_out), .in13(XOR_out), .out(ALUResult), .sel(ALUCtl));  // open: in3, in4, in5, in8, in9, in10, in11, in14, in15
  Comparator #(.width(32)) comparator_2 (.a(ALUResult), .b({32{1'b0}}), .eq(Zero));  // open: gt, lt
endmodule

module Register_File (
  input  [4:0] in_1,
  input  [4:0] in_2,
  input  in_3,
  input  [4:0] in_4,
  input  [31:0] in_5,
  input  in_6,
  output [31:0] out_7,
  output [31:0] out_8
);

  wire and_1_out, and_2_out, comparator_1_eq, comparator_2_eq, comparator_3_eq, comparator_4_eq,
       decoder_1_out1, decoder_1_out2, decoder_1_out3, decoder_1_out4, decoder_1_out5, decoder_1_out6,
       decoder_1_out7, decoder_1_out8, decoder_1_out9, decoder_1_out10, decoder_1_out11, decoder_1_out12,
       decoder_1_out13, decoder_1_out14, decoder_1_out15, decoder_1_out16, decoder_1_out17, decoder_1_out18,
       decoder_1_out19, decoder_1_out20, decoder_1_out21, decoder_1_out22, decoder_1_out23, decoder_1_out24,
       decoder_1_out25, decoder_1_out26, decoder_1_out27, decoder_1_out28, decoder_1_out29, decoder_1_out30,
       decoder_1_out31;
  wire [31:0] multiplexer_1_out, multiplexer_3_out, register_1_q, register_2_q, register_3_q, register_4_q,
       register_5_q, register_6_q, register_7_q, register_8_q, register_9_q, register_10_q, register_11_q,
       register_12_q, register_13_q, register_14_q, register_15_q, register_16_q, register_17_q,
       register_18_q, register_19_q, register_20_q, register_21_q, register_22_q, register_23_q,
       register_24_q, register_25_q, register_26_q, register_27_q, register_28_q, register_29_q,
       register_30_q, register_31_q;

  Decoder #(.select(5), .disabled(0)) decoder_1 (
    .out1(decoder_1_out1), .out2(decoder_1_out2), .out3(decoder_1_out3), .out4(decoder_1_out4),
    .out5(decoder_1_out5), .out6(decoder_1_out6), .out7(decoder_1_out7), .out8(decoder_1_out8),
    .out9(decoder_1_out9), .out10(decoder_1_out10), .out11(decoder_1_out11), .out12(decoder_1_out12),
    .out13(decoder_1_out13), .out14(decoder_1_out14), .out15(decoder_1_out15), .out16(decoder_1_out16),
    .out17(decoder_1_out17), .out18(decoder_1_out18), .out19(decoder_1_out19), .out20(decoder_1_out20),
    .out21(decoder_1_out21), .out22(decoder_1_out22), .out23(decoder_1_out23), .out24(decoder_1_out24),
    .out25(decoder_1_out25), .out26(decoder_1_out26), .out27(decoder_1_out27), .out28(decoder_1_out28),
    .out29(decoder_1_out29), .out30(decoder_1_out30), .out31(decoder_1_out31), .sel(in_4), .en(in_3));  // open: out0
  Register #(.width(32)) register_1 (.D(in_5), .en(decoder_1_out3), .Q(register_1_q), .clk(in_6), .clr(1'b0));
  Register #(.width(32)) register_2 (.D(in_5), .en(decoder_1_out7), .Q(register_2_q), .clk(in_6), .clr(1'b0));
  Register #(.width(32)) register_3 (.D(in_5), .en(decoder_1_out11), .Q(register_3_q), .clk(in_6), .clr(1'b0));
  Register #(.width(32)) register_4 (.D(in_5), .en(decoder_1_out15), .Q(register_4_q), .clk(in_6), .clr(1'b0));
  Register #(.width(32)) register_5 (.D(in_5), .en(decoder_1_out19), .Q(register_5_q), .clk(in_6), .clr(1'b0));
  Register #(.width(32)) register_6 (.D(in_5), .en(decoder_1_out23), .Q(register_6_q), .clk(in_6), .clr(1'b0));
  Register #(.width(32)) register_7 (.D(in_5), .en(decoder_1_out27), .Q(register_7_q), .clk(in_6), .clr(1'b0));
  Register #(.width(32)) register_8 (.D(in_5), .en(decoder_1_out31), .Q(register_8_q), .clk(in_6), .clr(1'b0));
  Register #(.width(32)) register_9 (.D(in_5), .en(decoder_1_out2), .Q(register_9_q), .clk(in_6), .clr(1'b0));
  Register #(.width(32)) register_10 (.D(in_5), .en(decoder_1_out6), .Q(register_10_q), .clk(in_6), .clr(1'b0));
  Register #(.width(32)) register_11 (.D(in_5), .en(decoder_1_out10), .Q(register_11_q), .clk(in_6), .clr(1'b0));
  Register #(.width(32)) register_12 (.D(in_5), .en(decoder_1_out14), .Q(register_12_q), .clk(in_6), .clr(1'b0));
  Register #(.width(32)) register_13 (.D(in_5), .en(decoder_1_out18), .Q(register_13_q), .clk(in_6), .clr(1'b0));
  Register #(.width(32)) register_14 (.D(in_5), .en(decoder_1_out22), .Q(register_14_q), .clk(in_6), .clr(1'b0));
  Register #(.width(32)) register_15 (.D(in_5), .en(decoder_1_out26), .Q(register_15_q), .clk(in_6), .clr(1'b0));
  Register #(.width(32)) register_16 (.D(in_5), .en(decoder_1_out30), .Q(register_16_q), .clk(in_6), .clr(1'b0));
  Register #(.width(32)) register_17 (.D(in_5), .en(decoder_1_out1), .Q(register_17_q), .clk(in_6), .clr(1'b0));
  Register #(.width(32)) register_18 (.D(in_5), .en(decoder_1_out5), .Q(register_18_q), .clk(in_6), .clr(1'b0));
  Register #(.width(32)) register_19 (.D(in_5), .en(decoder_1_out9), .Q(register_19_q), .clk(in_6), .clr(1'b0));
  Register #(.width(32)) register_20 (.D(in_5), .en(decoder_1_out13), .Q(register_20_q), .clk(in_6), .clr(1'b0));
  Register #(.width(32)) register_21 (.D(in_5), .en(decoder_1_out17), .Q(register_21_q), .clk(in_6), .clr(1'b0));
  Register #(.width(32)) register_22 (.D(in_5), .en(decoder_1_out21), .Q(register_22_q), .clk(in_6), .clr(1'b0));
  Register #(.width(32)) register_23 (.D(in_5), .en(decoder_1_out25), .Q(register_23_q), .clk(in_6), .clr(1'b0));
  Register #(.width(32)) register_24 (.D(in_5), .en(decoder_1_out29), .Q(register_24_q), .clk(in_6), .clr(1'b0));
  Register #(.width(32)) register_25 (.D(in_5), .en(decoder_1_out4), .Q(register_25_q), .clk(in_6), .clr(1'b0));
  Register #(.width(32)) register_26 (.D(in_5), .en(decoder_1_out8), .Q(register_26_q), .clk(in_6), .clr(1'b0));
  Register #(.width(32)) register_27 (.D(in_5), .en(decoder_1_out12), .Q(register_27_q), .clk(in_6), .clr(1'b0));
  Register #(.width(32)) register_28 (.D(in_5), .en(decoder_1_out16), .Q(register_28_q), .clk(in_6), .clr(1'b0));
  Register #(.width(32)) register_29 (.D(in_5), .en(decoder_1_out20), .Q(register_29_q), .clk(in_6), .clr(1'b0));
  Register #(.width(32)) register_30 (.D(in_5), .en(decoder_1_out24), .Q(register_30_q), .clk(in_6), .clr(1'b0));
  Register #(.width(32)) register_31 (.D(in_5), .en(decoder_1_out28), .Q(register_31_q), .clk(in_6), .clr(1'b0));
  Comparator #(.width(5)) comparator_1 (.a({5{1'b0}}), .b(in_1), .eq(comparator_1_eq));  // open: gt, lt
  Comparator #(.width(5)) comparator_2 (.a(in_1), .b(in_4), .eq(comparator_2_eq));  // open: gt, lt
  and and_1 (and_1_out, in_3, ~comparator_1_eq, comparator_2_eq);  // AND_Gate
  Multiplexer #(.select(5), .width(32), .enable("false")) multiplexer_1 (
    .in0({32{1'b0}}), .in1(register_17_q), .in2(register_9_q), .in3(register_1_q), .in4(register_25_q),
    .in5(register_18_q), .in6(register_10_q), .in7(register_2_q), .in8(register_26_q), .in9(register_19_q),
    .in10(register_11_q), .in11(register_3_q), .in12(register_27_q), .in13(register_20_q),
    .in14(register_12_q), .in15(register_4_q), .in16(register_28_q), .in17(register_21_q),
    .in18(register_13_q), .in19(register_5_q), .in20(register_29_q), .in21(register_22_q),
    .in22(register_14_q), .in23(register_6_q), .in24(register_30_q), .in25(register_23_q),
    .in26(register_15_q), .in27(register_7_q), .in28(register_31_q), .in29(register_24_q),
    .in30(register_16_q), .in31(register_8_q), .out(multiplexer_1_out), .sel(in_1));
  Multiplexer #(.width(32), .disabled(0), .enable("false")) multiplexer_2 (
    .in0(multiplexer_1_out), .in1(in_5), .out(out_7), .sel(and_1_out));
  Multiplexer #(.select(5), .width(32), .enable("false")) multiplexer_3 (
    .in0({32{1'b0}}), .in1(register_17_q), .in2(register_9_q), .in3(register_1_q), .in4(register_25_q),
    .in5(register_18_q), .in6(register_10_q), .in7(register_2_q), .in8(register_26_q), .in9(register_19_q),
    .in10(register_11_q), .in11(register_3_q), .in12(register_27_q), .in13(register_20_q),
    .in14(register_12_q), .in15(register_4_q), .in16(register_28_q), .in17(register_21_q),
    .in18(register_13_q), .in19(register_5_q), .in20(register_29_q), .in21(register_22_q),
    .in22(register_14_q), .in23(register_6_q), .in24(register_30_q), .in25(register_23_q),
    .in26(register_15_q), .in27(register_7_q), .in28(register_31_q), .in29(register_24_q),
    .in30(register_16_q), .in31(register_8_q), .out(multiplexer_3_out), .sel(in_2));
  Multiplexer #(.width(32), .disabled(0), .enable("false")) multiplexer_4 (
    .in0(multiplexer_3_out), .in1(in_5), .out(out_8), .sel(and_2_out));
  and and_2 (and_2_out, ~comparator_3_eq, comparator_4_eq, in_3);  // AND_Gate
  Comparator #(.width(5)) comparator_3 (.a({5{1'b0}}), .b(in_2), .eq(comparator_3_eq));  // open: gt, lt
  Comparator #(.width(5)) comparator_4 (.a(in_2), .b(in_4), .eq(comparator_4_eq));  // open: gt, lt

  // Other names for the same wires on the sheet: RegWrite = in_3; WriteData[31:0] = in_5; WriteReg[4:0] = in_4
endmodule
