// Logisim project pipelined_mips.circ as structural Verilog: 22 circuits, main circuit Pipelined MIPS
module Pipelined_MIPS (
  output [31:0] IF_PC,
  output [31:0] IF_Instr,
  output [31:0] ID_RegRs,
  output [31:0] ID_RegRt,
  output [31:0] EX_ALUA,
  output [31:0] EX_ALUB,
  output [3:0] EX_ALUCtl,
  output [31:0] MEM_MemData,
  output MEM_MemRead,
  output MEM_MemWrite,
  output [31:0] WB_RegData,
  output WB_RegWrite
);

  wire alu_1_zero, and_1_out, clock_1_out, control_1_alusrc, control_1_branch, control_1_memread,
       control_1_memtoreg, control_1_memwrite, control_1_regdst, control_1_regwrite, ex_mem_1_out_15,
       ex_mem_1_out_17, ex_mem_1_out_19, ex_mem_1_out_20, id_ex_1_out_18, id_ex_1_out_19, id_ex_1_out_20,
       id_ex_1_out_21, id_ex_1_out_23, id_ex_1_out_24, id_ex_1_out_25, mem_wb_1_out_9, stall1_1_not_stall;
  wire [1:0] control_1_aluop, forward_1_forwarda, forward_1_forwardb, id_ex_1_out_22;
  wire [4:0] ex_mem_1_out_23, id_ex_1_out_30, id_ex_1_out_31, mem_wb_1_out_11, multiplexer_3_out, rd_1_out_2,
       register_3_q, rs_1_out_2, rt_1_out_2;
  wire [5:0] funct_1_out_2, opcode_1_out_2;
  wire [6:0] low7_1_out_2, low7_2_out_2;
  wire [15:0] imm_1_out_2;
  wire [31:0] adder_1_out, adder_2_out, alu_1_aluresult, dm_1_out_6, ex_mem_1_out_14, ex_mem_1_out_21,
       id_ex_1_out_26, id_ex_1_out_27, id_ex_1_out_28, id_ex_1_out_29, ls2_1_out_2, mem_wb_1_out_12,
       mem_wb_1_out_13, multiplexer_1_out, multiplexer_2_out, multiplexer_5_out, register_1_q, register_2_q,
       rs2_1_out_2, rs2_2_out_2, se_1_out_2;

  Multiplexer #(.width(32), .enable("false")) multiplexer_1 (
    .in0(IF_PC), .in1(multiplexer_2_out), .out(multiplexer_1_out), .sel(stall1_1_not_stall));
  Multiplexer #(.width(32), .enable("false")) multiplexer_2 (
    .in0(adder_1_out), .in1(ex_mem_1_out_14), .out(multiplexer_2_out), .sel(and_1_out));
  PC pc_1 (.in_1(multiplexer_1_out), .out_2(IF_PC));
  Adder #(.width(32)) adder_1 (.a(32'h4), .b(IF_PC), .out(adder_1_out));  // open: cin, cout
  rs2 rs2_1 (.in_1(IF_PC), .out_2(rs2_1_out_2));
  low7 low7_1 (.in_1(rs2_1_out_2), .out_2(low7_1_out_2));
  IM im_1 (.in_1(low7_1_out_2), .out_2(IF_Instr));
  Clock clock_1 (.out(clock_1_out));
  Register #(.width(32)) register_1 (
    .D(adder_1_out), .en(stall1_1_not_stall), .Q(register_1_q), .clk(clock_1_out), .clr(1'b0));
  Register #(.width(32)) register_2 (
    .D(IF_Instr), .en(stall1_1_not_stall), .Q(register_2_q), .clk(clock_1_out), .clr(1'b0));
  opcode opcode_1 (.in_1(register_2_q), .out_2(opcode_1_out_2));
  rs rs_1 (.in_1(register_2_q), .out_2(rs_1_out_2));
  rt rt_1 (.in_1(register_2_q), .out_2(rt_1_out_2));
  imm imm_1 (.in_1(register_2_q), .out_2(imm_1_out_2));
  rd rd_1 (.in_1(register_2_q), .out_2(rd_1_out_2));
  Register_File register_file_1 (
    .in_1(rs_1_out_2), .in_3(WB_RegWrite), .in_5(WB_RegData), .out_7(ID_RegRs), .out_8(ID_RegRt),
    .in_4(mem_wb_1_out_11), .in_6(clock_1_out), .in_2(rt_1_out_2));
  se se_1 (.in_1(imm_1_out_2), .out_2(se_1_out_2));
  control control_1 (
    .in_1(opcode_1_out_2), .RegDst(control_1_regdst), .Branch(control_1_branch), .MemRead(control_1_memread),
    .MemtoReg(control_1_memtoreg), .ALUOp(control_1_aluop), .MemWrite(control_1_memwrite),
    .ALUSrc(control_1_alusrc), .RegWrite(control_1_regwrite));
  ID_EX id_ex_1 (
    .in_1(control_1_regdst), .in_2(control_1_branch), .in_3(control_1_memread), .in_4(control_1_memtoreg),
    .in_5(control_1_aluop), .in_6(control_1_memwrite), .in_7(control_1_alusrc), .in_8(control_1_regwrite),
    .in_9(register_1_q), .in_10(ID_RegRs), .in_11(ID_RegRt), .in_12(se_1_out_2), .in_13(rt_1_out_2),
    .in_14(rd_1_out_2), .out_18(id_ex_1_out_18), .out_19(id_ex_1_out_19), .out_20(id_ex_1_out_20),
    .out_21(id_ex_1_out_21), .out_22(id_ex_1_out_22), .out_23(id_ex_1_out_23), .out_24(id_ex_1_out_24),
    .out_25(id_ex_1_out_25), .out_26(id_ex_1_out_26), .out_27(id_ex_1_out_27), .out_28(id_ex_1_out_28),
    .out_29(id_ex_1_out_29), .out_30(id_ex_1_out_30), .out_31(id_ex_1_out_31), .in_15(stall1_1_not_stall),
    .in_16(clock_1_out), .in_17(1'b0));
  Register #(.width(5)) register_3 (.D(rs_1_out_2), .en(1'b1), .Q(register_3_q), .clk(clock_1_out), .clr(1'b0));
  ls2 ls2_1 (.in_1(id_ex_1_out_29), .out_2(ls2_1_out_2));
  funct funct_1 (.in_1(id_ex_1_out_29), .out_2(funct_1_out_2));
  Multiplexer #(.width(5), .enable("false")) multiplexer_3 (
    .in0(id_ex_1_out_30), .in1(id_ex_1_out_31), .out(multiplexer_3_out), .sel(id_ex_1_out_18));
  Adder #(.width(32)) adder_2 (.a(id_ex_1_out_26), .b(ls2_1_out_2), .out(adder_2_out));  // open: cin, cout
  Multiplexer #(.select(2), .width(32), .disabled(0), .enable("false")) multiplexer_4 (
    .in0(id_ex_1_out_27), .in1(ex_mem_1_out_21), .in2(WB_RegData), .out(EX_ALUA), .sel(forward_1_forwarda));  // open: in3
  Multiplexer #(.select(2), .width(32), .disabled(0), .enable("false")) multiplexer_5 (
    .in0(id_ex_1_out_28), .in1(ex_mem_1_out_21), .in2(WB_RegData), .out(multiplexer_5_out),
    .sel(forward_1_forwardb));  // open: in3
  ALU alu_1 (.A(EX_ALUA), .B(EX_ALUB), .ALUResult(alu_1_aluresult), .Zero(alu_1_zero), .ALUCtl(EX_ALUCtl));
  Multiplexer #(.width(32), .enable("false")) multiplexer_6 (
    .in0(multiplexer_5_out), .in1(id_ex_1_out_29), .out(EX_ALUB), .sel(id_ex_1_out_24));
  alu_control alu_control_1 (.funct(funct_1_out_2), .ALUOp(id_ex_1_out_22), .ALU(EX_ALUCtl));
  forward forward_1 (
    .ForwardA(forward_1_forwarda), .ForwardB(forward_1_forwardb), .rs_s3(register_3_q),
    .rt_s3(id_ex_1_out_30), .regwrite_s4(ex_mem_1_out_19), .regwrite_s5(WB_RegWrite),
    .wrreg_s4(ex_mem_1_out_23), .wrreg_s5(mem_wb_1_out_11));
  stall1 stall1_1 (
    .memread_s3(id_ex_1_out_20), .rs_s2(rs_1_out_2), .rt_s2(rt_1_out_2), .rt_s3(id_ex_1_out_30),
    .not_stall(stall1_1_not_stall));
  EX_MEM ex_mem_1 (
    .in_1(adder_2_out), .in_2(id_ex_1_out_19), .in_3(id_ex_1_out_20), .in_4(id_ex_1_out_21),
    .in_5(id_ex_1_out_23), .in_6(id_ex_1_out_25), .in_7(alu_1_zero), .in_8(alu_1_aluresult),
    .in_10(multiplexer_3_out), .out_14(ex_mem_1_out_14), .out_15(ex_mem_1_out_15), .out_16(MEM_MemRead),
    .out_17(ex_mem_1_out_17), .out_18(MEM_MemWrite), .out_19(ex_mem_1_out_19), .out_20(ex_mem_1_out_20),
    .out_21(ex_mem_1_out_21), .out_23(ex_mem_1_out_23), .in_11(1'b1), .in_12(clock_1_out), .in_13(1'b0),
    .in_9(multiplexer_5_out), .out_22(MEM_MemData));
  and and_1 (and_1_out, ex_mem_1_out_15, ex_mem_1_out_20);
  rs2 rs2_2 (.in_1(ex_mem_1_out_21), .out_2(rs2_2_out_2));
  low7 low7_2 (.in_1(rs2_2_out_2), .out_2(low7_2_out_2));
  DM dm_1 (
    .in_2(low7_2_out_2), .in_3(MEM_MemData), .out_6(dm_1_out_6), .write(MEM_MemWrite), .clk(clock_1_out),
    .read(MEM_MemRead));
  MEM_WB mem_wb_1 (
    .in_1(ex_mem_1_out_17), .in_2(ex_mem_1_out_19), .in_3(ex_mem_1_out_23), .in_5(dm_1_out_6),
    .out_9(mem_wb_1_out_9), .out_10(WB_RegWrite), .out_11(mem_wb_1_out_11), .out_13(mem_wb_1_out_13),
    .in_6(1'b1), .in_7(clock_1_out), .in_8(1'b0), .in_4(ex_mem_1_out_21), .out_12(mem_wb_1_out_12));
  Multiplexer #(.width(32), .enable("false")) multiplexer_7 (
    .in0(mem_wb_1_out_12), .in1(mem_wb_1_out_13), .out(WB_RegData), .sel(mem_wb_1_out_9));

  // Other names for the same wires on the sheet: _01[31:0] = IF_PC; _02[31:0] = IF_Instr; _03[31:0] = ID_RegRs;
  //   _04[31:0] = ID_RegRt; _05[31:0] = EX_ALUA; _06[31:0] = EX_ALUB; _07[3:0] = EX_ALUCtl; _08[31:0] = MEM_MemData;
  //   _09 = MEM_MemRead; _10 = MEM_MemWrite; _11[31:0] = WB_RegData; _12 = WB_RegWrite
endmodule

module ID_EX (
  input  in_1,
  input  in_2,
  input  in_3,
  input  in_4,
  input  [1:0] in_5,
  input  in_6,
  input  in_7,
  input  in_8,
  input  [31:0] in_9,
  input  [31:0] in_10,
  input  [31:0] in_11,
  input  [31:0] in_12,
  input  [4:0] in_13,
  input  [4:0] in_14,
  input  in_15,
  input  in_16,
  input  in_17,
  output out_18,
  output out_19,
  output out_20,
  output out_21,
  output [1:0] out_22,
  output out_23,
  output out_24,
  output out_25,
  output [31:0] out_26,
  output [31:0] out_27,
  output [31:0] out_28,
  output [31:0] out_29,
  output [4:0] out_30,
  output [4:0] out_31
);

  Register #(.width(9)) register_1 (
    .D({in_8, in_7, in_6, in_5, in_4, in_3, in_2, in_1}), .en(in_15),
    .Q({out_25, out_24, out_23, out_22, out_21, out_20, out_19, out_18}), .clk(in_16), .clr(in_17));
  Register #(.width(32)) register_2 (.D(in_9), .en(in_15), .Q(out_26), .clk(in_16), .clr(in_17));
  Register #(.width(32)) register_3 (.D(in_10), .en(in_15), .Q(out_27), .clk(in_16), .clr(in_17));
  Register #(.width(32)) register_4 (.D(in_11), .en(in_15), .Q(out_28), .clk(in_16), .clr(in_17));
  Register #(.width(32)) register_5 (.D(in_12), .en(in_15), .Q(out_29), .clk(in_16), .clr(in_17));
  Register #(.width(5)) register_6 (.D(in_13), .en(in_15), .Q(out_30), .clk(in_16), .clr(in_17));
  Register #(.width(5)) register_7 (.D(in_14), .en(in_15), .Q(out_31), .clk(in_16), .clr(in_17));
endmodule

module EX_MEM (
  input  [31:0] in_1,
  input  in_2,
  input  in_3,
  input  in_4,
  input  in_5,
  input  in_6,
  input  in_7,
  input  [31:0] in_8,
  input  [31:0] in_9,
  input  [4:0] in_10,
  input  in_11,
  input  in_12,
  input  in_13,
  output [31:0] out_14,
  output out_15,
  output out_16,
  output out_17,
  output out_18,
  output out_19,
  output out_20,
  output [31:0] out_21,
  output [31:0] out_22,
  output [4:0] out_23
);

  Register #(.width(32)) register_1 (.D(in_1), .en(in_11), .Q(out_14), .clk(in_12), .clr(in_13));
  Register #(.width(6)) register_2 (
    .D({in_7, in_6, in_5, in_4, in_3, in_2}), .en(in_11),
    .Q({out_20, out_19, out_18, out_17, out_16, out_15}), .clk(in_12), .clr(in_13));
  Register #(.width(32)) register_3 (.D(in_8), .en(in_11), .Q(out_21), .clk(in_12), .clr(in_13));
  Register #(.width(32)) register_4 (.D(in_9), .en(in_11), .Q(out_22), .clk(in_12), .clr(in_13));
  Register #(.width(5)) register_5 (.D(in_10), .en(in_11), .Q(out_23), .clk(in_12), .clr(in_13));
endmodule

module MEM_WB (
  input  in_1,
  input  in_2,
  input  [4:0] in_3,
  input  [31:0] in_4,
  input  [31:0] in_5,
  input  in_6,
  input  in_7,
  input  in_8,
  output out_9,
  output out_10,
  output [4:0] out_11,
  output [31:0] out_12,
  output [31:0] out_13
);

  Register #(.width(7)) register_1 (
    .D({in_3, in_2, in_1}), .en(in_6), .Q({out_11, out_10, out_9}), .clk(in_7), .clr(in_8));
  Register #(.width(32)) register_2 (.D(in_4), .en(in_6), .Q(out_12), .clk(in_7), .clr(in_8));
  Register #(.width(32)) register_3 (.D(in_5), .en(in_6), .Q(out_13), .clk(in_7), .clr(in_8));
endmodule

module PC (
  input  [31:0] in_1,
  output [31:0] out_2
);

  wire clock_1_out;

  Register #(.width(32)) register_1 (.D(in_1), .en(1'b1), .Q(out_2), .clk(clock_1_out), .clr(1'b0));
  Clock clock_1 (.out(clock_1_out));
endmodule

module rs2 (
  input  [31:0] in_1,
  output [31:0] out_2
);


  assign out_2 = {2'b00, in_1[31:2]};
endmodule

module low7 (
  input  [31:0] in_1,
  output [6:0] out_2
);


  assign out_2 = in_1[6:0];
endmodule

module IM (
  input  [6:0] in_1,
  output [31:0] out_2
);

  RAM #(.addrWidth(7), .dataWidth(32), .bus("asynch")) ram_1 (
    .addr(in_1), .data(out_2), .sel(1'b1), .ld(1'b1), .clr(1'b0));

  // Notes on the sheet:
  //   Instruction Memory
endmodule

module rs (
  input  [31:0] in_1,
  output [4:0] out_2
);


  assign out_2 = in_1[25:21];
endmodule

module rt (
  input  [31:0] in_1,
  output [4:0] out_2
);


  assign out_2 = in_1[20:16];
endmodule

module imm (
  input  [31:0] in_1,
  output [15:0] out_2
);


  assign out_2 = in_1[15:0];
endmodule

module se (
  input  [15:0] in_1,
  output [31:0] out_2
);


  assign out_2 = {{17{in_1[15]}}, in_1[14:0]};

  // Notes on the sheet:
  //   sign extend 16-bit to 32-bit
endmodule

module rd (
  input  [31:0] in_1,
  output [4:0] out_2
);


  assign out_2 = in_1[15:11];
endmodule

module opcode (
  input  [31:0] in_1,
  output [5:0] out_2
);


  assign out_2 = in_1[31:26];
endmodule

module control (
  input  [5:0] in_1,
  output RegDst,
  output Branch,
  output MemRead,
  output MemtoReg,
  output [1:0] ALUOp,
  output MemWrite,
  output ALUSrc,
  output RegWrite
);

  wire and_1_out, and_2_out, and_6_out, and_7_out, and_8_out, and_10_out, and_11_out, and_12_out, and_13_out,
       and_14_out;

  and and_1 (and_1_out, in_1[0], in_1[1], ~in_1[2], ~in_1[3], ~in_1[4], in_1[5]);  // AND_Gate
  and and_2 (and_2_out, ~in_1[0], ~in_1[1], ~in_1[2], in_1[3], ~in_1[4], ~in_1[5]);  // AND_Gate
  and and_3 (Branch, ~in_1[0], ~in_1[1], in_1[2], ~in_1[3], ~in_1[4], ~in_1[5]);  // AND_Gate
  and and_4 (MemRead, in_1[0], in_1[1], ~in_1[2], ~in_1[3], ~in_1[4], in_1[5]);  // AND_Gate
  and and_5 (ALUOp[0], ~in_1[0], ~in_1[1], in_1[2], ~in_1[3], ~in_1[4], ~in_1[5]);  // AND_Gate
  and and_6 (and_6_out, in_1[0], in_1[1], ~in_1[2], ~in_1[3], ~in_1[4], in_1[5]);  // AND_Gate
  and and_7 (and_7_out, in_1[0], in_1[1], ~in_1[2], in_1[3], ~in_1[4], in_1[5]);  // AND_Gate
  and and_8 (and_8_out, ~in_1[0], ~in_1[1], ~in_1[2], in_1[3], ~in_1[4], ~in_1[5]);  // AND_Gate
  and and_9 (MemWrite, in_1[0], in_1[1], ~in_1[2], in_1[3], ~in_1[4], in_1[5]);  // AND_Gate
  and and_10 (and_10_out, in_1[0], in_1[1], ~in_1[2], ~in_1[3], ~in_1[4], in_1[5]);  // AND_Gate
  and and_11 (and_11_out, in_1[0], in_1[1], ~in_1[2], in_1[3], ~in_1[4], in_1[5]);  // AND_Gate
  and and_12 (and_12_out, ~in_1[0], ~in_1[1], ~in_1[2], in_1[3], ~in_1[4], ~in_1[5]);  // AND_Gate
  and and_13 (and_13_out, ~in_1[0], ~in_1[1], in_1[2], ~in_1[3], ~in_1[4], ~in_1[5]);  // AND_Gate
  and and_14 (and_14_out, in_1[0], in_1[1], ~in_1[2], in_1[3], ~in_1[4], in_1[5]);  // AND_Gate
  nor nor_1 (RegDst, and_1_out, and_2_out);
  nor nor_2 (ALUOp[1], ALUOp[0], and_6_out, and_7_out, and_8_out);
  nor nor_3 (RegWrite, and_13_out, and_14_out);
  or or_1 (ALUSrc, and_10_out, and_11_out, and_12_out);

  assign MemtoReg = MemRead;
endmodule

module ls2 (
  input  [31:0] in_1,
  output [31:0] out_2
);


  assign out_2 = {in_1[29:0], 2'b00};
endmodule

module funct (
  input  [31:0] in_1,
  output [5:0] out_2
);


  assign out_2 = in_1[5:0];
endmodule

module alu_control (
  input  [5:0] funct,
  input  [1:0] ALUOp,
  output [3:0] ALU
);

  wire [3:0] multiplexer_1_out;

  Multiplexer #(.select(4), .width(4), .enable("false")) multiplexer_1 (
    .in0(4'b0010), .in1(4'b0000), .in2(4'b0110), .in3(4'b0000), .in4(4'b0000), .in5(4'b0001), .in6(4'b1101),
    .in7(4'b1100), .in8(4'b0000), .in9(4'b0000), .in10(4'b0111), .in11(4'b0000), .in12(4'b0000),
    .in13(4'b0000), .in14(4'b0000), .in15(4'b0000), .out(multiplexer_1_out), .sel(funct[3:0]));
  Multiplexer #(.select(2), .width(4), .enable("false")) multiplexer_2 (
    .in0(4'b0010), .in1(4'b0110), .in2(multiplexer_1_out), .in3(4'b0010), .out(ALU), .sel(ALUOp));
endmodule

module DM (
  input  write,
  input  [6:0] in_2,
  input  [31:0] in_3,
  input  clk,
  input  read,
  output [31:0] out_6
);

  RAM #(.addrWidth(7), .dataWidth(32), .bus("separate")) ram_1 (
    .addr(in_2), .din(in_3), .data(out_6), .str(write), .sel(1'b1), .clk(clk), .ld(read), .clr(1'b0));

  // Notes on the sheet:
  //   Address
  //   128 words (512 bytes)
  //   write data
  //   read data
endmodule

module forward (
  input  regwrite_s4,
  input  regwrite_s5,
  input  [4:0] rs_s3,
  input  [4:0] wrreg_s4,
  input  [4:0] rt_s3,
  input  [4:0] wrreg_s5,
  output [1:0] ForwardA,
  output [1:0] ForwardB
);

  wire and_1_out, and_2_out, and_3_out, and_4_out, eq5_1_out_3, eq5_2_out_3, eq5_3_out_3, eq5_4_out_3;
  wire [1:0] multiplexer_1_out, multiplexer_2_out;

  eq5 eq5_1 (.in_1(wrreg_s5), .in_2(rs_s3), .out_3(eq5_1_out_3));
  eq5 eq5_2 (.in_1(wrreg_s5), .in_2(rt_s3), .out_3(eq5_2_out_3));
  Multiplexer #(.width(2), .disabled(0), .enable("false")) multiplexer_1 (
    .in0(2'b00), .in1(2'b10), .out(multiplexer_1_out), .sel(and_1_out));
  and and_1 (and_1_out, eq5_1_out_3, regwrite_s5);
  eq5 eq5_3 (.in_1(wrreg_s4), .in_2(rs_s3), .out_3(eq5_3_out_3));
  Multiplexer #(.width(2), .disabled(0), .enable("false")) multiplexer_2 (
    .in0(2'b00), .in1(2'b10), .out(multiplexer_2_out), .sel(and_2_out));
  and and_2 (and_2_out, eq5_2_out_3, regwrite_s5);
  eq5 eq5_4 (.in_1(wrreg_s4), .in_2(rt_s3), .out_3(eq5_4_out_3));
  Multiplexer #(.width(2), .disabled(0), .enable("false")) multiplexer_3 (
    .in0(multiplexer_1_out), .in1(2'b01), .out(ForwardA), .sel(and_3_out));
  and and_3 (and_3_out, eq5_3_out_3, regwrite_s4);
  Multiplexer #(.width(2), .disabled(0), .enable("false")) multiplexer_4 (
    .in0(multiplexer_2_out), .in1(2'b01), .out(ForwardB), .sel(and_4_out));
  and and_4 (and_4_out, eq5_4_out_3, regwrite_s4);

  // Notes on the sheet:
  //   s5
  //   s5
  //   s4
  //   s4
endmodule

module eq5 (
  input  [4:0] in_1,
  input  [4:0] in_2,
  output out_3
);

  wire [4:0] xnor_1_out;

  assign xnor_1_out = ~(in_1 ^ in_2);  // XNOR_Gate xnor_1, 5 bits wide
  and and_1 (out_3, xnor_1_out[0], xnor_1_out[1], xnor_1_out[2], xnor_1_out[3], xnor_1_out[4]);
endmodule

module stall1 (
  input  memread_s3,
  input  [4:0] rs_s2,
  input  [4:0] rt_s2,
  input  [4:0] rt_s3,
  output not_stall
);

  wire and_1_out, eq5_1_out_3, eq5_2_out_3, or_1_out;

  eq5 eq5_1 (.in_1(rs_s2), .in_2(rt_s3), .out_3(eq5_1_out_3));
  eq5 eq5_2 (.in_1(rt_s2), .in_2(rt_s3), .out_3(eq5_2_out_3));
  or or_1 (or_1_out, eq5_1_out_3, eq5_2_out_3);
  and and_1 (and_1_out, memread_s3, or_1_out);
  not not_1 (not_stall, and_1_out);
endmodule
